# Fritzing sketch 5_button (saved by Fritzing 0.9.9b)
breadboards: 1

parts:
  Pico_H1 = Raspberry Pi Pico H
  LED1 = smd LED [color="Blue (430nm)" package="0603 [SMD]"]
  S1 = Pushbutton [package="[THT]"]

nets:
  N1: Pico_H1.GND, LED1.cathode
  N2: Pico_H1.3V3, S1.Pin_3, S1.Pin_4
  N3: LED1.anode, S1.Pin_1, S1.Pin_2

notes:
  slot on bottom of switch goes up and down

custom parts:
  Raspberry Pi Pico H: Raspberry Pi Pico H. Based around the RP2040 microcontroller the Pico H is a low cost microcontroller device bringing Raspberry Pi quality, cost, and easy of use to the microcontroller space.
