# Fritzing sketch 7_blink_external (saved by Fritzing 0.9.9b)
breadboards: 1

parts:
  Pico_H1 = Raspberry Pi Pico H
  LED1 = smd LED [color="Blue (430nm)" package="0603 [SMD]"]

nets:
  N1: Pico_H1.GND, LED1.cathode
  N2: Pico_H1.GP16, LED1.anode

custom parts:
  Raspberry Pi Pico H: Raspberry Pi Pico H. Based around the RP2040 microcontroller the Pico H is a low cost microcontroller device bringing Raspberry Pi quality, cost, and easy of use to the microcontroller space.
