# Fritzing sketch game_1_lab (saved by Fritzing 0.9.9b)
breadboards: 1

parts:
  Pico_H1 = Raspberry Pi Pico H
  R1 = PHOTOCELL [package=photocell-kit]
  R2 = Resistor [tolerance=±5% resistance=10k package="1206 [SMD]"]
  S1 = Pushbutton [package="[THT]"]

nets:
  N1: Pico_H1.GND, R2.Pin_0
  N2: Pico_H1.3V3, R1.P$2, S1.Pin_1, S1.Pin_2
  N3: Pico_H1.GP28_A2, R1.P$1, R2.Pin_1
  N4: Pico_H1.GP17, S1.Pin_3, S1.Pin_4

notes:
  10K
  Photo-resistor
  Target
  To Laser

custom parts:
  Raspberry Pi Pico H: Raspberry Pi Pico H. Based around the RP2040 microcontroller the Pico H is a low cost microcontroller device bringing Raspberry Pi quality, cost, and easy of use to the microcontroller space.
