# Fritzing sketch game_2_lab (saved by Fritzing 0.9.9b)
breadboards: 1

parts:
  R3 = PHOTOCELL [package=photocell-kit]
  R4 = Resistor [tolerance=±5% resistance=10k package="1206 [SMD]"]
  M4 = Dagu DGServo 9g (Top view) [part_number=RS001B]
  Pico_H2 = Raspberry Pi Pico H
  S2 = Pushbutton [package="[THT]"]
  LED1 = smd LED [color="Blue (430nm)" package="1206 [SMD]"]
  LED2 = smd LED [color="White (8000K)" package="1206 [SMD]"]
  LED3 = smd LED [color="Green (555nm)" package="1206 [SMD]"]

nets:
  N1: R3.P$1, R4.Pin_1, Pico_H2.GP28_A2
  N2: R3.P$2, Pico_H2.3V3, S2.Pin_1, S2.Pin_2
  GND: R4.Pin_0, M4.gnd, Pico_H2.GND, LED1.cathode, LED2.cathode, LED3.cathode
  N3: M4.vcc, Pico_H2.VBUS
  N4: M4.pulse, Pico_H2.GP15
  N5: Pico_H2.GP19, LED1.anode
  N6: Pico_H2.GP18, LED2.anode
  N7: Pico_H2.GP17, S2.Pin_3, S2.Pin_4
  N8: Pico_H2.GP16, LED3.anode

notes:
  10K
  Photo-resistor
  Target
  To Laser
  Shark On here
  LED long legs connect to Pico. Short legs to ground(-) rail.

custom parts:
  Raspberry Pi Pico H: Raspberry Pi Pico H. Based around the RP2040 microcontroller the Pico H is a low cost microcontroller device bringing Raspberry Pi quality, cost, and easy of use to the microcontroller space.
