# Fritzing sketch joystick 2 (saved by Fritzing 0.9.3b)
breadboards: 1

parts:
  Pico_H1 = Raspberry Pi Pico H
  Mod1 = KY-023 Dual Axis Joystick Module [package="Breakout board"]

nets:
  N1: Pico_H1.VBUS, Mod1.+5V
  GND: Pico_H1.GND, Mod1.GND
  N2: Pico_H1.GP27_A1, Mod1.VRx
  N3: Pico_H1.GP26_A0, Mod1.VRy
  N4: Pico_H1.GP17, Mod1.SW

custom parts:
  Raspberry Pi Pico H: Raspberry Pi Pico H. Based around the RP2040 microcontroller the Pico H is a low cost microcontroller device bringing Raspberry Pi quality, cost, and easy of use to the microcontroller space.
  KY-023 Dual Axis Joystick Module: KY-023 Dual-Axis Joystick Module.
