# Fritzing sketch servo_with_led_pico (saved by Fritzing 0.9.9b)
breadboards: 1

parts:
  Pico_H1 = Raspberry Pi Pico H
  M2 = Dagu DGServo 9g (Top view) [part_number=RS001B]
  LED1 = smd LED [color="Blue (430nm)" package="1206 [SMD]"]

nets:
  N1: Pico_H1.VBUS, M2.vcc
  GND: Pico_H1.GND, M2.gnd, LED1.cathode
  N2: Pico_H1.GP16, LED1.anode
  N3: Pico_H1.GP15, M2.pulse

notes:
  5volts
  orange/yellow wire is signal wire
  sg90 servo

custom parts:
  Raspberry Pi Pico H: Raspberry Pi Pico H. Based around the RP2040 microcontroller the Pico H is a low cost microcontroller device bringing Raspberry Pi quality, cost, and easy of use to the microcontroller space.
